// Logisim project PROJECT.circ as structural Verilog: 1 circuit, main circuit main
module main (
  input  KEY_CODE,
  input  in_2,
  input  in_3,
  input  DATA_ENTRY,
  input  in_5,
  input  in_6,
  output _7
);

  wire nor_1_out, nor_2_out, nor_3_out, xor_1_out, xor_2_out, xor_3_out;

  xor xor_1 (xor_1_out, KEY_CODE, DATA_ENTRY);
  xor xor_2 (xor_2_out, in_2, in_5);
  xor xor_3 (xor_3_out, in_3, in_6);
  nor nor_1 (nor_1_out, xor_1_out, xor_1_out);
  nor nor_2 (nor_2_out, xor_2_out, xor_2_out);
  nor nor_3 (nor_3_out, xor_3_out, xor_3_out);
  and and_1 (_7, nor_1_out, nor_2_out, nor_3_out);

  // Notes on the sheet:
  //   1
  //   2
  //   3
  //   4
  //   5
  //   6
  //   BUZZER
endmodule
